// Logisim project 1_circuito.circ as structural Verilog: 1 circuit, main circuit main
module main (
  input  A,
  input  B,
  input  C,
  output out_4
);

  wire and_1_out, xor_1_out;

  and and_1 (and_1_out, A, B);
  xor xor_1 (xor_1_out, A, C);
  or or_1 (out_4, and_1_out, xor_1_out);

  // Notes on the sheet:
  //   Meu primeiro circuito
endmodule
