// Logisim project Ex_01.circ as structural Verilog: 1 circuit, main circuit main
module main (
  input  X,
  input  Y,
  input  Z,
  output S
);

  wire and_1_out;

  and and_1 (and_1_out, ~Y, Z);  // AND_Gate
  or or_1 (S, X, and_1_out);

  // Notes on the sheet:
  //   Circuito combinacional S=X+Y'.Z
endmodule
