// Logisim project Ex_01_2.circ as structural Verilog: 1 circuit, main circuit main
module main (
  input  A,
  input  B,
  output S
);

  wire nand_1_out, nor_1_out;

  nand nand_1 (nand_1_out, A, B);
  nor nor_1 (nor_1_out, A, B);
  or or_1 (S, nand_1_out, nor_1_out);

  // Notes on the sheet:
  //   Exercício 1
endmodule
