// Logisim project Ex_02.circ as structural Verilog: 1 circuit, main circuit main
module main (
  input  A,
  input  B,
  input  C,
  output S
);

  wire and_1_out, and_2_out, nor_1_out;

  and and_1 (and_1_out, ~A, B);  // AND_Gate
  nor nor_1 (nor_1_out, A, C);
  and and_2 (and_2_out, B, nor_1_out);
  or or_1 (S, and_1_out, and_2_out);

  // Notes on the sheet:
  //   Circuito combinacional S=A'.B+B.(A+C)'
endmodule
