// Logisim project Ex_02_2.circ as structural Verilog: 1 circuit, main circuit main
module main (
  input  A,
  input  B,
  input  C,
  output out_4
);

  wire and_1_out, nand_1_out;

  nand nand_1 (nand_1_out, B, C);
  and and_1 (and_1_out, A, nand_1_out);
  nand nand_2 (out_4, A, and_1_out);

  // Notes on the sheet:
  //   Exercício 2
endmodule
