// Logisim project Ex_03.circ as structural Verilog: 1 circuit, main circuit main
module main (
  input  A,
  input  B,
  input  C,
  input  D,
  output S
);

  wire or_1_out, or_2_out, or_3_out, or_4_out;

  or or_1 (or_1_out, B, D);
  or or_2 (or_2_out, A, C);
  or or_3 (or_3_out, B, C);
  or or_4 (or_4_out, A, D);
  and and_1 (S, or_1_out, or_2_out, or_3_out, or_4_out);

  // Notes on the sheet:
  //   Exercício 3
endmodule
