// Logisim project Ex_04.circ as structural Verilog: 1 circuit, main circuit main
module main (
  input  A,
  input  B,
  input  C,
  input  D,
  input  E,
  output out_6
);

  wire and_1_out, and_2_out, and_3_out, and_4_out, nor_1_out, or_1_out, or_2_out, or_3_out;

  and and_1 (and_1_out, ~E, D, C);  // AND_Gate
  and and_2 (and_2_out, B, C);
  nor nor_1 (nor_1_out, B, D);
  or or_1 (or_1_out, B, D);
  or or_2 (or_2_out, and_1_out, and_2_out);
  or or_3 (or_3_out, nor_1_out, or_1_out);
  and and_3 (and_3_out, or_2_out, A);
  and and_4 (and_4_out, or_3_out, A);
  or or_4 (out_6, and_3_out, and_4_out);

  // Notes on the sheet:
  //   Exercício 4
endmodule
