// Logisim project Ex_10.circ as structural Verilog: 1 circuit, main circuit main
module main (
  input  A,
  input  B,
  input  C,
  input  D,
  output out_5
);

  or or_1 (out_5, A, B, C, D);
endmodule
