// Logisim project Ex_12.circ as structural Verilog: 1 circuit, main circuit main
module main (
  input  D,
  input  C,
  input  B,
  input  A
);

  wire and_1_out, and_2_out, and_3_out, and_4_out, and_5_out, and_6_out, and_7_out, and_8_out, and_9_out,
       and_10_out, and_11_out, and_12_out, or_1_out, or_2_out, or_3_out, or_4_out, or_5_out, or_6_out,
       or_7_out, xnor_1_out, xnor_2_out;

  xnor xnor_1 (xnor_1_out, C, A);
  xnor xnor_2 (xnor_2_out, A, B);
  or or_1 (or_1_out, A, ~B, C, D);  // OR_Gate
  and and_1 (and_1_out, C, ~B, A);  // AND_Gate
  and and_2 (and_2_out, ~A, B);  // AND_Gate
  and and_3 (and_3_out, ~D, B, ~C);  // AND_Gate
  and and_4 (and_4_out, ~C, ~A);  // AND_Gate
  and and_5 (and_5_out, ~A, ~C);  // AND_Gate
  and and_6 (and_6_out, ~A, B);  // AND_Gate
  and and_7 (and_7_out, ~A, ~B);  // AND_Gate
  and and_8 (and_8_out, C, ~B);  // AND_Gate
  and and_9 (and_9_out, C, B, ~A);  // AND_Gate
  and and_10 (and_10_out, B, ~A);  // AND_Gate
  and and_11 (and_11_out, C, ~B);  // AND_Gate
  and and_12 (and_12_out, ~D, ~C, B);  // AND_Gate
  or or_2 (or_2_out, xnor_1_out, B, D);
  or or_3 (or_3_out, xnor_2_out, ~C, D);  // OR_Gate
  or or_4 (or_4_out, and_1_out, and_2_out, and_3_out, and_4_out);
  or or_5 (or_5_out, and_5_out, and_6_out);
  or or_6 (or_6_out, and_7_out, and_8_out, and_9_out, D);
  or or_7 (or_7_out, and_10_out, and_11_out, and_12_out, D);
  _7_Segment_Display u_7_segment_display_1 (
    .g(or_7_out), .f(or_6_out), .a(or_2_out), .b(or_3_out), .e(or_5_out), .d(or_4_out), .c(or_1_out));  // open: dp
endmodule
