// Logisim project Ex_13.circ as structural Verilog: 1 circuit, main circuit main
module main (
  input  A,
  input  B,
  input  C,
  input  D,
  output out_5,
  output out_6,
  output out_7,
  output out_8
);

  wire and_1_out, and_2_out, and_3_out, and_4_out, and_5_out, and_6_out;

  and and_1 (and_1_out, B, ~C);  // AND_Gate
  and and_2 (and_2_out, ~A, ~B, C);  // AND_Gate
  and and_3 (and_3_out, A, ~B, C);  // AND_Gate
  and and_4 (and_4_out, A, C);
  and and_5 (and_5_out, B, C);
  and and_6 (and_6_out, ~A, ~B, D);  // AND_Gate
  xor xor_1 (out_6, A, B);
  or or_1 (out_7, and_1_out, and_2_out, and_3_out);
  or or_2 (out_8, C, and_4_out, and_5_out, and_6_out);

  assign out_5 = A;
endmodule
