// Logisim project Ex_14.circ as structural Verilog: 1 circuit, main circuit main
module main (
  input  E0,
  input  E0_2,
  input  E1,
  input  E1_2,
  input  E2,
  input  E2_2,
  input  E3,
  input  E3_2,
  input  E4,
  input  E4_2,
  input  E5,
  input  E5_2,
  input  E6,
  input  E6_2,
  input  E7,
  input  E7_2,
  input  E8,
  input  E8_2,
  input  E9,
  input  E9_2,
  input  E10,
  input  E10_2,
  input  E11,
  input  E11_2,
  input  E12,
  input  E12_2,
  input  E13,
  input  E13_2,
  input  E14,
  input  E14_2,
  input  E15,
  input  E15_2,
  input  [1:0] CD,
  input  [1:0] AB,
  input  [3:0] AB_2,
  output out_36,
  output out_37
);

  wire multiplexer_1_out, multiplexer_2_out, multiplexer_3_out, multiplexer_4_out;

  Multiplexer #(.select(2), .enable("false")) multiplexer_1 (
    .in0(E0), .in1(E1), .in2(E2), .in3(E3), .out(multiplexer_1_out), .sel(AB));
  Multiplexer #(.select(2), .enable("false")) multiplexer_2 (
    .in0(E4), .in1(E5), .in2(E6), .in3(E7), .out(multiplexer_2_out), .sel(AB));
  Multiplexer #(.select(2), .enable("false")) multiplexer_3 (
    .in0(E8), .in1(E9), .in2(E10), .in3(E11), .out(multiplexer_3_out), .sel(AB));
  Multiplexer #(.select(2), .enable("false")) multiplexer_4 (
    .in0(E12), .in1(E13), .in2(E14), .in3(E15), .out(multiplexer_4_out), .sel(AB));
  Multiplexer #(.select(2), .enable("false")) multiplexer_5 (
    .in0(multiplexer_1_out), .in1(multiplexer_2_out), .in2(multiplexer_3_out), .in3(multiplexer_4_out),
    .out(out_36), .sel(CD));
  Multiplexer #(.select(4), .enable("false")) multiplexer_6 (
    .in0(E0_2), .in1(E1_2), .in2(E2_2), .in3(E3_2), .in4(E4_2), .in5(E5_2), .in6(E6_2), .in7(E7_2),
    .in8(E8_2), .in9(E9_2), .in10(E10_2), .in11(E11_2), .in12(E12_2), .in13(E13_2), .in14(E14_2),
    .in15(E15_2), .out(out_37), .sel(AB_2));

  // Notes on the sheet:
  //   MUX 16 CANAIS COM MUX DE 4 CANAIS
endmodule
