// Logisim project Ex_15.circ as structural Verilog: 1 circuit, main circuit main
module main (
  input  in_1,
  input  [1:0] in_2,
  input  [1:0] in_3,
  output E0,
  output E1,
  output E2,
  output E3,
  output E4,
  output E5,
  output E6,
  output E7,
  output E8,
  output E9,
  output E10,
  output E11,
  output E12,
  output E13,
  output E14,
  output E15
);

  wire demultiplexer_1_out0, demultiplexer_1_out1, demultiplexer_1_out2, demultiplexer_1_out3;

  Demultiplexer #(.select(2), .enable("false")) demultiplexer_1 (
    .out0(demultiplexer_1_out0), .out1(demultiplexer_1_out1), .out2(demultiplexer_1_out2),
    .out3(demultiplexer_1_out3), .in(in_1), .sel(in_2));
  Demultiplexer #(.select(2), .enable("false")) demultiplexer_2 (
    .out0(E0), .out1(E1), .out2(E2), .out3(E3), .in(demultiplexer_1_out0), .sel(in_3));
  Demultiplexer #(.select(2), .enable("false")) demultiplexer_3 (
    .out0(E4), .out1(E5), .out2(E6), .out3(E7), .in(demultiplexer_1_out1), .sel(in_3));
  Demultiplexer #(.select(2), .enable("false")) demultiplexer_4 (
    .out0(E8), .out1(E9), .out2(E10), .out3(E11), .in(demultiplexer_1_out2), .sel(in_3));
  Demultiplexer #(.select(2), .enable("false")) demultiplexer_5 (
    .out0(E12), .out1(E13), .out2(E14), .out3(E15), .in(demultiplexer_1_out3), .sel(in_3));

  // Notes on the sheet:
  //   DEMUX 16 CANAIS COM DEMUX DE 4 CANAIS
endmodule
