// Logisim project Porta lógica OR - 2 entradas.circ as structural Verilog: 1 circuit, main circuit main
module main (
  input  A,
  input  B,
  output S
);

  or or_1 (S, A, B);

  // Notes on the sheet:
  //   Porta OR - 2 entradas
endmodule
