// Logisim project adders_subtractors.circ as structural Verilog: 1 circuit, main circuit main
module main (
  input  A,
  input  A_2,
  input  B,
  input  B_2,
  input  m,
  input  A_3,
  input  B_3,
  input  Ci,
  input  Bi,
  input  A_4,
  input  A_5,
  input  B_4,
  input  B_5,
  input  m_2,
  input  [3:0] A_6,
  input  [3:0] A1_A_2_A3_A4,
  input  [3:0] B_6,
  input  [3:0] B1_B2_B3_B4,
  output out_19,
  output S,
  output out_21,
  output Bo,
  output S_2,
  output Co_Bo,
  output S_3,
  output S_4,
  output Co,
  output Bo_2,
  output S_5,
  output [3:0] S1_S2_S3_S4,
  output Bo_3,
  output Co_Bo_2
);

  wire adder_3_cout, adder_4_cout, xor_1_out;
  wire [3:0] xor_2_out;
  wire [3:1] adder_4_out;

  Adder #(.width(1)) adder_1 (.a(A), .b(B), .out(out_19), .cout(out_21));  // open: cin
  Adder #(.width(1)) adder_2 (.a(A_4), .b(B_4), .out(S_3), .cin(Ci), .cout(Co));
  Subtractor #(.width(1)) subtractor_1 (.a(A_2), .b(B_2), .out(S), .bout(Bo));  // open: bin
  Subtractor #(.width(1)) subtractor_2 (.a(A_5), .b(B_5), .out(S_4), .bin(Bi), .bout(Bo_2));
  Subtractor #(.width(4)) subtractor_3 (
    .a(A1_A_2_A3_A4), .b(B1_B2_B3_B4), .out(S1_S2_S3_S4), .bout(Bo_3));  // open: bin
  xor xor_1 (xor_1_out, m, B_3);
  xor xor_2 (xor_2_out[0], m_2, B_6[0]);
  Adder #(.width(1)) adder_3 (.a(A_3), .b(xor_1_out), .out(S_2), .cin(m), .cout(adder_3_cout));
  xor xor_3 (Co_Bo, adder_3_cout, m);
  Adder #(.width(4)) adder_4 (.a(A_6), .b(xor_2_out), .out({adder_4_out, S_5}), .cin(m_2), .cout(adder_4_cout));
  xor xor_4 (Co_Bo_2, adder_4_cout, m_2);
  // Pins of 1 and 4 bits meet at xor_2_out
  // Pins of 1 and 4 bits meet at {adder_4_out, S_5}
  // Pins of 1 and 4 bits meet at B_6

  // Notes on the sheet:
  //   Half Adder 1 bit
  //   Full Adder 1 bit
  //   Half Subtractor 1 bit
  //   Full Subtractor 1 bit
  //   Half Subtractor 4 bits
  //   Full Adder 1 bit ex3
  //   Full Adder 1 bit ex3
endmodule
