// Logisim project binaryToExcesso3.circ as structural Verilog: 1 circuit, main circuit main
module main (
  input  A,
  input  B,
  input  C,
  input  D,
  output W,
  output X,
  output Y,
  output Y_2
);

  wire and_1_out, and_2_out, and_3_out, and_4_out, and_5_out, and_6_out, and_7_out, and_8_out, and_9_out;

  and and_1 (and_1_out, C, B);
  and and_2 (and_2_out, D, B);
  and and_3 (and_3_out, B, ~C, ~D);  // AND_Gate
  and and_4 (and_4_out, ~B, D);  // AND_Gate
  and and_5 (and_5_out, ~B, C);  // AND_Gate
  and and_6 (and_6_out, ~C, ~D);  // AND_Gate
  and and_7 (and_7_out, C, D);
  and and_8 (and_8_out, ~C, ~D);  // AND_Gate
  and and_9 (and_9_out, C, ~D);  // AND_Gate
  or or_1 (W, A, and_1_out, and_2_out);
  or or_2 (X, and_3_out, and_4_out, and_5_out);
  or or_3 (Y, and_6_out, and_7_out);
  or or_4 (Y_2, and_8_out, and_9_out);
endmodule
