// Logisim project binaryToGray.circ as structural Verilog: 1 circuit, main circuit main
module main (
  input  A,
  input  B,
  input  C,
  input  D,
  output W,
  output X,
  output Y,
  output Z
);

  xor xor_1 (X, A, B);
  xor xor_2 (Y, B, C);
  xor xor_3 (Z, D, C);

  assign W = A;
endmodule
