// Logisim project display_7_segmentos.circ as structural Verilog: 1 circuit, main circuit main
module main (
  input  D,
  input  C,
  input  B,
  input  A,
  input  in_5
);

  wire and_1_out, and_2_out, and_3_out, and_4_out, and_5_out, and_6_out, and_7_out, and_8_out, and_9_out,
       and_10_out, or_1_out, or_2_out, or_3_out, or_4_out, or_5_out, or_6_out, or_7_out, or_8_out,
       xnor_1_out, xnor_2_out, xor_1_out;

  or or_1 (or_1_out, D, B);
  xnor xnor_1 (xnor_1_out, C, A);
  xnor xnor_2 (xnor_2_out, B, A);
  or or_2 (or_2_out, ~B, A, C, D);  // OR_Gate
  and and_1 (and_1_out, ~C, ~A);  // AND_Gate
  and and_2 (and_2_out, B, ~A);  // AND_Gate
  and and_3 (and_3_out, C, ~B, A);  // AND_Gate
  and and_4 (and_4_out, B, ~C);  // AND_Gate
  and and_5 (and_5_out, ~C, ~A);  // AND_Gate
  and and_6 (and_6_out, B, ~A);  // AND_Gate
  and and_7 (and_7_out, ~B, ~A);  // AND_Gate
  and and_8 (and_8_out, C, ~B);  // AND_Gate
  and and_9 (and_9_out, C, ~A);  // AND_Gate
  and and_10 (and_10_out, B, ~A);  // AND_Gate
  xor xor_1 (xor_1_out, B, C);
  or or_3 (or_3_out, or_1_out, xnor_1_out);
  or or_4 (or_4_out, ~C, xnor_2_out);  // OR_Gate
  or or_5 (or_5_out, and_1_out, D, and_2_out, and_3_out, and_4_out);
  or or_6 (or_6_out, and_5_out, and_6_out);
  or or_7 (or_7_out, and_7_out, D, and_8_out, and_9_out);
  or or_8 (or_8_out, and_10_out, D, xor_1_out);
  _7_Segment_Display u_7_segment_display_1 (
    .g(or_8_out), .f(or_7_out), .a(or_3_out), .b(or_4_out), .e(or_6_out), .d(or_5_out), .c(or_2_out),
    .dp(in_5));
endmodule
