// Logisim project flip flop básico assíncrono.circ as structural Verilog: 1 circuit, main circuit main
module main (
  input  A,
  input  B,
  output Q1,
  output Q2
);

  nand nand_1 (Q1, ~A, Q2);  // NAND_Gate
  nand nand_2 (Q2, Q1, ~B);  // NAND_Gate

  // Notes on the sheet:
  //   FLIP FLOP SR SÍNCRONO
endmodule
