// Logisim project flip flop d.circ as structural Verilog: 1 circuit, main circuit main
module main (
  input  PRESET,
  input  A,
  input  CLEAR,
  output out_4,
  output out_5
);

  wire clock_1_out, nand_1_out, nand_2_out, nand_3_out, nand_4_out, nand_5_out, nand_6_out, not_1_out,
       not_2_out;

  Clock clock_1 (.out(clock_1_out));
  not not_1 (not_1_out, A);
  nand nand_1 (nand_1_out, out_5, A, clock_1_out);
  nand nand_2 (nand_2_out, clock_1_out, not_1_out, out_4);
  nand nand_3 (nand_3_out, PRESET, nand_1_out, nand_4_out);
  nand nand_4 (nand_4_out, nand_3_out, nand_2_out, CLEAR);
  not not_2 (not_2_out, clock_1_out);
  nand nand_5 (nand_5_out, nand_3_out, not_2_out);
  nand nand_6 (nand_6_out, not_2_out, nand_4_out);
  nand nand_7 (out_4, PRESET, nand_5_out, out_5);
  nand nand_8 (out_5, out_4, nand_6_out, CLEAR);

  // Notes on the sheet:
  //   FLIP FLOP D
endmodule
