// Logisim project flip flop rs assincrono.circ as structural Verilog: 1 circuit, main circuit main
module main (
  input  A,
  input  B,
  output Q1,
  output Q2
);

  nor nor_1 (Q1, A, Q2);
  nor nor_2 (Q2, Q1, B);

  // Notes on the sheet:
  //   FLIP FLOP RS ASSÍNCRONO
endmodule
