// Logisim project flip flop sr sincrono.circ as structural Verilog: 2 circuits, main circuit main
module main (
  input  A,
  input  B,
  output Q1,
  output Q2
);

  wire clock_1_out, nand_1_out, nand_2_out;

  Clock clock_1 (.out(clock_1_out));
  nand nand_1 (nand_1_out, A, clock_1_out);
  nand nand_2 (nand_2_out, clock_1_out, B);
  nand nand_3 (Q1, nand_1_out, Q2);
  nand nand_4 (Q2, Q1, nand_2_out);

  // Notes on the sheet:
  //   FLIP FLOP SR SÍNCRONO
endmodule

module FF_SR_SINCRONO (
  input  A,
  input  B,
  output Q1,
  output Q2
);

  wire clock_1_out, nand_1_out, nand_2_out;

  Clock clock_1 (.out(clock_1_out));
  nand nand_1 (nand_1_out, A, clock_1_out);
  nand nand_2 (nand_2_out, clock_1_out, B);
  nand nand_3 (Q1, nand_1_out, Q2);
  nand nand_4 (Q2, Q1, nand_2_out);
endmodule
