// Logisim project mux_demux.circ as structural Verilog: 1 circuit, main circuit main
module main (
  input  E0,
  input  E1,
  input  in_3,
  input  E2,
  input  E3,
  input  [1:0] A,
  input  in_7,
  input  in_8,
  input  [1:0] in_9,
  input  [1:0] in_10,
  input  [1:0] in_11,
  input  [1:0] in_12,
  input  [1:0] in_13,
  input  [1:0] in_14,
  output S0,
  output S0_2,
  output S1,
  output S1_2,
  output S,
  output S2,
  output S2_2,
  output S3,
  output S3_2,
  output S4,
  output S4_2,
  output S5,
  output S5_2,
  output S6,
  output S0_3,
  output S6_2,
  output S7,
  output S1_3,
  output S7_2,
  output S2_3,
  output S3_3,
  output S8,
  output S9,
  output S10,
  output S11,
  output S12,
  output S13,
  output S14,
  output S15
);

  wire demultiplexer_2_out0, demultiplexer_2_out1, demultiplexer_5_out0, demultiplexer_5_out1,
       demultiplexer_6_out0, demultiplexer_6_out1, demultiplexer_7_out0, demultiplexer_7_out1;

  Demultiplexer #(.select(2), .enable("false")) demultiplexer_1 (
    .out0(S0_3), .out1(S1_3), .out2(S2_3), .out3(S3_3), .in(in_8), .sel(in_11));
  Multiplexer #(.select(2), .enable("false")) multiplexer_1 (.in0(E0), .in1(E1), .in2(E2), .in3(E3), .out(S), .sel(A));
  Demultiplexer #(.select(2), .enable("false")) demultiplexer_2 (
    .out0(demultiplexer_2_out0), .out1(demultiplexer_2_out1), .in(in_3), .sel(in_9));  // open: out2, out3
  Demultiplexer #(.select(2), .enable("false")) demultiplexer_3 (
    .out0(S0), .out1(S1), .out2(S2), .out3(S3), .in(demultiplexer_2_out0), .sel(in_10));
  Demultiplexer #(.select(2), .enable("false")) demultiplexer_4 (
    .out0(S4), .out1(S5), .out2(S6), .out3(S7), .in(demultiplexer_2_out1), .sel(in_10));
  Demultiplexer #(.select(2), .enable("false")) demultiplexer_5 (
    .out0(demultiplexer_5_out0), .out1(demultiplexer_5_out1), .in(in_7), .sel(in_12));  // open: out2, out3
  Demultiplexer #(.select(2), .enable("false")) demultiplexer_6 (
    .out0(demultiplexer_6_out0), .out1(demultiplexer_6_out1), .in(demultiplexer_5_out0), .sel(in_13));  // open: out2, out3
  Demultiplexer #(.select(2), .enable("false")) demultiplexer_7 (
    .out0(demultiplexer_7_out0), .out1(demultiplexer_7_out1), .in(demultiplexer_5_out1), .sel(in_13));  // open: out2, out3
  Demultiplexer #(.select(2), .enable("false")) demultiplexer_8 (
    .out0(S0_2), .out1(S1_2), .out2(S2_2), .out3(S3_2), .in(demultiplexer_6_out0), .sel(in_14));
  Demultiplexer #(.select(2), .enable("false")) demultiplexer_9 (
    .out0(S4_2), .out1(S5_2), .out2(S6_2), .out3(S7_2), .in(demultiplexer_6_out1), .sel(in_14));
  Demultiplexer #(.select(2), .enable("false")) demultiplexer_10 (
    .out0(S8), .out1(S9), .out2(S10), .out3(S11), .in(demultiplexer_7_out0), .sel(in_14));
  Demultiplexer #(.select(2), .enable("false")) demultiplexer_11 (
    .out0(S12), .out1(S13), .out2(S14), .out3(S15), .in(demultiplexer_7_out1), .sel(in_14));
endmodule
